// Logisim project BIT A BIT 4 BITS.circ as structural Verilog: 1 circuit, main circuit main
// BIT A BIT
module main (
  input  A_0,
  input  A_1,
  input  A_2,
  input  A_3,
  input  B_0,
  input  B_1,
  input  B_2,
  input  B_3,
  output NAND_0,
  output NAND_1,
  output NAND_2,
  output NAND_3,
  output NOR_0,
  output NOR_1,
  output NOR_2,
  output NOR_3,
  output XOR_0,
  output XOR_1,
  output XOR_2,
  output XOR_3
);

  BIT_A_BIT_main main_1 (.A(A_0), .B(B_0), .NAND(NAND_0), .NOR(NOR_0), .XOR(XOR_0));
  BIT_A_BIT_main main_2 (.A(A_1), .B(B_1), .NAND(NAND_1), .NOR(NOR_1), .XOR(XOR_1));
  BIT_A_BIT_main main_3 (.A(A_2), .B(B_2), .NAND(NAND_2), .NOR(NOR_2), .XOR(XOR_2));
  BIT_A_BIT_main main_4 (.A(A_3), .B(B_3), .NAND(NAND_3), .NOR(NOR_3), .XOR(XOR_3));
endmodule
