// Logisim project DESLOCAMENTO 4 BITS.circ as structural Verilog: 1 circuit, main circuit main
// DESL
module main (
  input  D_3,
  input  D_2,
  input  D_1,
  input  D_0,
  input  S_0,
  input  S1,
  output Y_3,
  output Y_2,
  output Y_1,
  output Y_0
);

  wire main_1_dy_meio_2, main_1_not_s1, main_1_s1, main_2_dy_anterior, main_2_dy_proximo, main_2_not_s1_2,
       main_2_s1_2, main_3_dy_anterior, main_3_dy_proximo, main_3_not_s1_2, main_4_dy_proximo;

  FIM_main main_1 (
    .S_0(S_0), .S_1(S1), .D_3(D_3), .Q_3(Y_3), .S1(main_1_s1), .NOT_S1(main_1_not_s1),
    .DY_MEIO(main_2_dy_proximo), .DY_MEIO_2(main_1_dy_meio_2));
  MEIO_main main_2 (
    .S1(main_1_s1), .NOT_S1(main_1_not_s1), .DY_PROXIMO(main_2_dy_proximo), .YD_PROXIMO(main_1_dy_meio_2),
    .D_2(D_2), .Q_2(Y_2), .S1_2(main_2_s1_2), .NOT_S1_2(main_2_not_s1_2), .YD_ANTERIOR(main_3_dy_proximo),
    .DY_ANTERIOR(main_2_dy_anterior));
  MEIO_main main_3 (
    .S1(main_2_s1_2), .NOT_S1(main_2_not_s1_2), .DY_PROXIMO(main_3_dy_proximo),
    .YD_PROXIMO(main_2_dy_anterior), .D_2(D_1), .Q_2(Y_1), .NOT_S1_2(main_3_not_s1_2),
    .YD_ANTERIOR(main_4_dy_proximo), .DY_ANTERIOR(main_3_dy_anterior));  // open: S1_2
  \INÍCIO_main  main_4 (
    .NOT_S1(main_3_not_s1_2), .DY_PROXIMO(main_4_dy_proximo), .DY_MEIO(main_3_dy_anterior), .D_0(D_0),
    .Q_0(Y_0));
endmodule
