// Logisim project FIM.circ as structural Verilog: 1 circuit, main circuit main
// FIM
module main (
  input  D_3,
  input  S_0,
  input  S_1,
  input  DY_MEIO,
  output S1,
  output NOT_S1,
  output DY_MEIO_2,
  output Q_3
);

  wire _1_out;

  not _11 (NOT_S1, S_1);
  and _2 (DY_MEIO_2, D_3, S_1);
  and _1 (_1_out, S_1, S_0, D_3);
  or _8 (Q_3, _1_out, DY_MEIO);

  assign S1 = S_1;
endmodule
