// Logisim project INÍCIO.circ as structural Verilog: 1 circuit, main circuit main
// INÍC
module main (
  input  D_0,
  input  NOT_S1,
  input  DY_MEIO,
  output DY_PROXIMO,
  output Q_0
);

  and _7 (DY_PROXIMO, NOT_S1, D_0);

  assign Q_0 = DY_MEIO;
endmodule
