// Logisim project MEIO.circ as structural Verilog: 1 circuit, main circuit main
// MEIO
module main (
  input  D_2,
  input  S1,
  input  NOT_S1,
  input  YD_ANTERIOR,
  input  YD_PROXIMO,
  output S1_2,
  output NOT_S1_2,
  output DY_PROXIMO,
  output DY_ANTERIOR,
  output Q_2
);

  and _3 (DY_PROXIMO, NOT_S1, D_2);
  and _4 (DY_ANTERIOR, D_2, S1);
  or _9 (Q_2, YD_PROXIMO, YD_ANTERIOR);

  assign NOT_S1_2 = NOT_S1;
  assign S1_2 = S1;
endmodule
