// Logisim project MUX 2 X 1 4 BITS.circ as structural Verilog: 1 circuit, main circuit main
// M 2 X 1
module main (
  input  B_3,
  input  B_2,
  input  B_1,
  input  B_0,
  input  A_3,
  input  A_2,
  input  A_1,
  input  A_0,
  input  S,
  output Y_3,
  output Y_2,
  output Y_1,
  output Y_0
);

  MUX_2_X_1_main main_1 (.E_1(A_3), .E_2(B_3), .S(S), .Y(Y_3));
  MUX_2_X_1_main main_2 (.E_1(A_2), .E_2(B_2), .S(S), .Y(Y_2));
  MUX_2_X_1_main main_3 (.E_1(A_1), .E_2(B_1), .S(S), .Y(Y_1));
  MUX_2_X_1_main main_4 (.E_1(A_0), .E_2(B_0), .S(S), .Y(Y_0));
endmodule
