// Logisim project MUX 4 X 1 4 BITS.circ as structural Verilog: 1 circuit, main circuit main
// MUX 4 X 1
module main (
  input  E_3,
  input  E_2,
  input  E_1,
  input  E_0,
  input  C_3,
  input  C_2,
  input  C_1,
  input  C_0,
  input  B_3,
  input  B_2,
  input  B_1,
  input  B_0,
  input  A_3,
  input  A_2,
  input  A_1,
  input  A_0,
  input  S_1,
  input  S_0,
  output Y_2,
  output Y_2_2,
  output Y_1,
  output Y_0
);

  MUX_4_X_1_main main_1 (.E_1(A_3), .E_2(B_3), .E_3(C_3), .E_4(E_3), .S1(S_1), .S0(S_0), .Y(Y_2));
  MUX_4_X_1_main main_2 (.E_1(A_2), .E_2(B_2), .E_3(C_2), .E_4(E_2), .S1(S_1), .S0(S_0), .Y(Y_2_2));
  MUX_4_X_1_main main_3 (.E_1(A_1), .E_2(B_1), .E_3(C_1), .E_4(E_1), .S1(S_1), .S0(S_0), .Y(Y_1));
  MUX_4_X_1_main main_4 (.E_1(A_0), .E_2(B_0), .E_3(C_0), .E_4(E_0), .S1(S_1), .S0(S_0), .Y(Y_0));
endmodule
