// Logisim project ULA 4 BITS.circ as structural Verilog: 1 circuit, main circuit main
module main (
  input  Cin,
  input  S_3,
  input  S_2,
  input  S_1,
  input  S_0,
  input  A_0,
  input  A_1,
  input  A_2,
  input  A_3,
  input  B_0,
  input  B_1,
  input  B_2,
  input  B_3,
  output Q_0,
  output Q_1,
  output Q_2,
  output Q_3,
  output Cout,
  output OVER_FLOW,
  output A___B,
  output A___0,
  output B___0,
  output A___B_2,
  output A___B_3
);

  wire main_1_nand_0, main_1_nand_1, main_1_nand_2, main_1_nand_3, main_1_nor_0, main_1_nor_1, main_1_nor_2,
       main_1_nor_3, main_1_xor_0, main_1_xor_1, main_1_xor_2, main_1_xor_3, main_2_c_3, main_2_q_0,
       main_2_q_1, main_2_q_2, main_2_q_3, main_3_y_0, main_3_y_1, main_3_y_2, main_3_y_3, main_5_y_0,
       main_5_y_1, main_5_y_2, main_5_y_3, undriven, undriven_2, undriven_3, undriven_4;

  BIT_A_BIT_4_BITS_main main_1 (
    .A_0(A_0), .A_1(A_1), .A_2(A_2), .A_3(A_3), .B_0(B_0), .B_1(B_1), .B_2(B_2), .B_3(B_3),
    .NAND_0(main_1_nand_0), .NAND_1(main_1_nand_1), .NAND_2(main_1_nand_2), .NAND_3(main_1_nand_3),
    .NOR_0(main_1_nor_0), .NOR_1(main_1_nor_1), .NOR_2(main_1_nor_2), .NOR_3(main_1_nor_3),
    .XOR_0(main_1_xor_0), .XOR_1(main_1_xor_1), .XOR_2(main_1_xor_2), .XOR_3(main_1_xor_3));
  \ARITMÉTICA_4_BITS_main  main_2 (
    .A_0(A_0), .B_0(B_0), .A_1(A_1), .B_1(B_1), .A_2(A_2), .B_2(B_2), .A_3(A_3), .B_3(B_3), .Cin(Cin),
    .S_0(S_1), .S_1(S_0), .Q_0(main_2_q_0), .Q_1(main_2_q_1), .Q_2(main_2_q_2), .Q_3(main_2_q_3),
    .C_3(main_2_c_3), .Cout(Cout));
  DESLOCAMENTO_4_BITS_main main_3 (
    .S_0(S_0), .S1(S_1), .D_3(A_3), .D_2(A_2), .D_1(A_1), .D_0(A_0), .Y_3(main_3_y_3), .Y_2(main_3_y_2),
    .Y_1(main_3_y_1), .Y_0(main_3_y_0));
  COMPARADOR_4_BITS_main main_4 (
    .A_0(A_0), .A_1(A_1), .A_2(A_2), .A_3(A_3), .B_0(B_0), .B_1(B_1), .B_2(B_2), .B_3(B_3), .Q_3(main_2_q_3),
    .Q_2(main_2_q_2), .Q_1(main_2_q_1), .Q_0(main_2_q_0), .Cout(Cout), .C_2(main_2_c_3),
    .OVER_FLOW(OVER_FLOW), .Q___0(A___B), .A___0(A___0), .A___B(A___B_2), .B___0(B___0), .A___B_2(A___B_3));
  XOR_4_BITS_main main_5 (
    .E_0(undriven), .E_1(undriven_2), .E_2(undriven_3), .E_3(undriven_4), .S_2(S_2), .Y_0(main_5_y_0),
    .Y_1(main_5_y_1), .Y_2(main_5_y_2), .Y_3(main_5_y_3));
endmodule
